// Logisim project DesigningAssignment_Aman22790.circ as structural Verilog: 1 circuit, main circuit main
module main (
  input  [15:0] in_1,
  input  [15:0] in_2,
  input  [7:0] in_3,
  input  [7:0] in_4,
  input  [7:0] in_5
);

  wire and_1_out, and_2_out, and_3_out, button_1_out, button_2_out, button_3_out, clock_1_out, clock_2_out,
       d_ff_1_q, j_k_ff_1_q, j_k_ff_1_qn, or_1_out, undriven;
  wire [7:0] adder_2_out, multiplexer_3_out, multiplexer_4_out, multiplexer_4_out_2, multiplexer_5_out,
       register_4_q, register_6_q, subtractor_1_out, undriven_2;
  wire [15:0] adder_1_out, demultiplexer_1_out0, demultiplexer_1_out1, demultiplexer_1_out2,
       demultiplexer_1_out4, demultiplexer_1_out5, multiplexer_1_out, multiplexer_2_out, ram_1_data,
       register_2_q, register_3_q;

  Clock clock_1 (.out(clock_1_out));
  Clock clock_2 (.out(clock_2_out));
  and and_1 (and_1_out, clock_2_out, d_ff_1_q);
  D_Flip_Flop d_ff_1 (.clk(button_1_out), .Q(d_ff_1_q), .reset(or_1_out));  // open: D, Qn, preset, en
  Button button_1 (.out(button_1_out));
  Demultiplexer #(.select(3), .width(16)) demultiplexer_1 (
    .out0(demultiplexer_1_out0), .out1(demultiplexer_1_out1), .out2(demultiplexer_1_out2),
    .out4(demultiplexer_1_out4), .out5(demultiplexer_1_out5), .in(in_1), .en(and_2_out));  // open: out3, out6, out7, sel
  J_K_Flip_Flop j_k_ff_1 (
    .J(and_1_out), .clk(and_1_out), .K(and_1_out), .Q(j_k_ff_1_q), .Qn(j_k_ff_1_qn), .en(button_2_out));  // open: preset, reset
  Button button_2 (.out(button_2_out));
  Multiplexer #(.width(16)) multiplexer_1 (
    .in0(register_2_q), .in1(demultiplexer_1_out2), .out(multiplexer_1_out));  // open: sel, en
  and and_2 (and_2_out, and_1_out, j_k_ff_1_q);
  and and_3 (and_3_out, j_k_ff_1_qn, and_1_out);
  or or_1 (or_1_out, demultiplexer_1_out4[15], undriven);
  Adder #(.width(16)) adder_1 (.a(multiplexer_1_out), .b(in_2), .out(adder_1_out));  // open: cin, cout
  Multiplexer #(.width(16)) multiplexer_2 (
    .in0(demultiplexer_1_out1), .in1(demultiplexer_1_out1), .out(multiplexer_2_out), .sel(and_3_out));  // open: en
  RAM #(.addrWidth(16), .dataWidth(16)) ram_1 (
    .addr(demultiplexer_1_out0), .data(ram_1_data), .clk(clock_1_out), .clr(button_3_out));  // open: sel, ld
  Register #(.width(16)) register_1 (
    .D(multiplexer_2_out), .Q(demultiplexer_1_out1), .clk(clock_1_out));  // open: en, clr
  Register #(.width(16)) register_2 (.D(adder_1_out), .Q(register_2_q), .clk(clock_1_out), .clr(undriven));  // open: en
  Register #(.width(16)) register_3 (.D(demultiplexer_1_out5), .Q(register_3_q), .clk(clock_1_out));  // open: en, clr
  Button button_3 (.out(button_3_out));
  Register register_4 (.D(multiplexer_4_out), .Q(register_4_q), .clk(clock_1_out));  // open: en, clr
  Adder adder_2 (.a(register_6_q), .b(register_3_q[7:0]), .out(adder_2_out));  // open: cin, cout
  Multiplexer #(.width(8)) multiplexer_3 (
    .in0(adder_2_out), .in1(subtractor_1_out), .out(multiplexer_3_out), .en(1'b1));  // open: sel
  Subtractor subtractor_1 (.a(register_6_q), .b(register_3_q[15:8]), .out(subtractor_1_out));  // open: bin, bout
  Register #(.width(16)) register_5 (.D({in_5, in_4}), .Q(demultiplexer_1_out5), .clk(1'b1));  // open: en, clr
  Multiplexer #(.select(3), .width(16)) multiplexer_4 (
    .in0(ram_1_data), .in1(demultiplexer_1_out1), .in2(register_2_q), .in3({register_4_q, in_3}),
    .in4({register_6_q, undriven_2}), .in5(register_3_q), .out({multiplexer_4_out_2, multiplexer_4_out}),
    .en(1'b1));  // open: in6, in7, sel
  Multiplexer #(.width(8)) multiplexer_5 (
    .in1(multiplexer_3_out), .out(multiplexer_5_out), .en(1'b1));  // open: in0, sel
  Register register_6 (.D(multiplexer_5_out), .Q(register_6_q), .clk(clock_1_out));  // open: en, clr

  // Notes on the sheet:
  //   AMAN RAZI KIDWAI 
  //   22790
  //   reset
  //   execute
  //   HALT
  //   0 TILL 7 BIT AS OUTPUT
  //   fetch
  //   RAM
  //   IR
  //   PC
  //   OUTPUT REGISTER
  //   Memory Buffer Register
  //   Clear
  //   Adder and subtractors
  //   Input register
  //   The output of INPR is the input of accumulator 
  //   accumulator
  //   IR
  //   PC
  //   OUTR
  //   INPR
  //   MBR
  //   AC
  //   List of registers added with RAM:
endmodule
